# Fritzing sketch nandeyanen_robot (saved by Fritzing 0.9.2b)
breadboards: 1

parts:
  Raspberry_Pi = Raspberry Pi 2
  5V_AC-DCアダプタより = Power plug
  J1 = Basic Servo
  音声合成モジュール = IC, DIP package, 28 pins [chip_label=ATP3011R4-PU]
  モノラルアンプ = mystery part, 6 pins [chip_label=AudioAmp]
  R1 = Rotary Potentiometer (Small) [maximum_resistance=100kΩ package=THT]
  SP1 = SPEAKER [package=pcb_mount_speaker]

nets:
  N1: Raspberry_Pi.GPIO2, 音声合成モジュール.pin27
  N2: Raspberry_Pi.GPIO3, 音声合成モジュール.pin28
  N3: Raspberry_Pi.GPIO21, J1.pulse
  GND: Raspberry_Pi.GND, 5V_AC-DCアダプタより.GND, J1.gnd, 音声合成モジュール.pin4, 音声合成モジュール.pin8, 音声合成モジュール.pin22, モノラルアンプ.pin5, モノラルアンプ.pin6, R1.leg1
  5V: Raspberry_Pi.5V, 5V_AC-DCアダプタより.VCC, J1.vcc, 音声合成モジュール.pin1, 音声合成モジュール.pin5, 音声合成モジュール.pin7, 音声合成モジュール.pin14, 音声合成モジュール.pin15, 音声合成モジュール.pin20, モノラルアンプ.pin1
  Audio Out: 音声合成モジュール.pin12, R1.leg2
  N4: モノラルアンプ.pin2, SP1.+
  N5: モノラルアンプ.pin3, SP1.-
  N6: モノラルアンプ.pin4, R1.wiper
